// Logisim project main.circ as structural Verilog: 1 circuit, main circuit main
module main (
);

  wire button_2_out, button_3_out, button_out, buttons_1_p2, buttons_1_p6, cdm_16_1_p2, cdm_16_1_p4,
       cdm_16_1_p5, cdm_16_1_p6, cdm_16_1_p7, decoder_1_pixel_state__bit_8, decoder_1_write__bit_9,
       not_1_out, ram_1_p4;
  wire [3:0] buttons_1_p5, cdm_16_1_p3, decoder_1_x_coord__bits_0_3, decoder_1_y_coord__bits_4_7;
  wire [15:0] cdm_16_1_p1, cdm_16_1_p8, cdm_16_1_p9, controlled_buffer_2_out, display_controller_1_c00,
       display_controller_1_c01, display_controller_1_c02, display_controller_1_c03,
       display_controller_1_c04, display_controller_1_c05, display_controller_1_c06,
       display_controller_1_c07, display_controller_1_c08, display_controller_1_c09,
       display_controller_1_c10, display_controller_1_c11, display_controller_1_c12,
       display_controller_1_c13, display_controller_1_c14, display_controller_1_c15;
  wire [15:4] cdm_16_1_p3_2;

  // Debugger debugger_1: pin names not known
  Button button (.out(button_out));
  Button button_2 (.out(button_2_out));
  Button button_3 (.out(button_3_out));
  // CdM_16 cdm_16_1: pin names not known; wires that end beside it: cdm_16_1_p1, cdm_16_1_p2, {cdm_16_1_p3_2, cdm_16_1_p3}, cdm_16_1_p4, cdm_16_1_p5, cdm_16_1_p6, cdm_16_1_p7, cdm_16_1_p8, cdm_16_1_p9
  decoder decoder_1 (
    .in_1(cdm_16_1_p1), .X_coord__bits_0_3(decoder_1_x_coord__bits_0_3),
    .Y_coord__bits_4_7(decoder_1_y_coord__bits_4_7), .pixel_state__bit_8(decoder_1_pixel_state__bit_8),
    .write__bit_9(decoder_1_write__bit_9));
  // Buttons buttons_1: pin names not known; wires that end beside it: button_out, buttons_1_p2, button_2_out, button_3_out, buttons_1_p5, buttons_1_p6
  Button button_4 (.out(buttons_1_p2));
  Clock clock_1 (.out(cdm_16_1_p2));
  DotMatrix #(.matrixcols(16), .matrixrows(16)) dotmatrix_1 (
    .col0(display_controller_1_c00), .col1(display_controller_1_c01), .col2(display_controller_1_c02),
    .col3(display_controller_1_c03), .col4(display_controller_1_c04), .col5(display_controller_1_c05),
    .col6(display_controller_1_c06), .col7(display_controller_1_c07), .col8(display_controller_1_c08),
    .col9(display_controller_1_c09), .col10(display_controller_1_c10), .col11(display_controller_1_c11),
    .col12(display_controller_1_c12), .col13(display_controller_1_c13), .col14(display_controller_1_c14),
    .col15(display_controller_1_c15));
  display_controller display_controller_1 (
    .X_coord(decoder_1_x_coord__bits_0_3), .Y_coord(decoder_1_y_coord__bits_4_7),
    .pixel_state(decoder_1_pixel_state__bit_8), .write(decoder_1_write__bit_9),
    .c00(display_controller_1_c00), .c01(display_controller_1_c01), .c02(display_controller_1_c02),
    .c03(display_controller_1_c03), .c04(display_controller_1_c04), .c05(display_controller_1_c05),
    .c06(display_controller_1_c06), .c07(display_controller_1_c07), .c08(display_controller_1_c08),
    .c09(display_controller_1_c09), .c10(display_controller_1_c10), .c11(display_controller_1_c11),
    .c12(display_controller_1_c12), .c13(display_controller_1_c13), .c14(display_controller_1_c14),
    .c15(display_controller_1_c15));  // open: pixel_check, checked, game_over
  assign cdm_16_1_p9 = cdm_16_1_p5 ? controlled_buffer_2_out : 16'bz;  // Controlled_Buffer controlled_buffer_1
  Register #(.width(4)) register_1 (.D(buttons_1_p5), .Q(cdm_16_1_p3), .clk(buttons_1_p6));  // open: en, clr
  assign controlled_buffer_2_out = not_1_out ? cdm_16_1_p8 : 16'bz;  // Controlled_Buffer controlled_buffer_2
  not not_1 (not_1_out, cdm_16_1_p5);
  // RAM ram_1: pin names not known; wires that end beside it: cdm_16_1_p7, cdm_16_1_p6, cdm_16_1_p4, ram_1_p4, cdm_16_1_p5, controlled_buffer_2_out
  Clock clock_2 (.out(ram_1_p4));

  // Notes on the sheet:
  //   Тут мы ставим кнопки для управления змеёй
  //   Тут мы ставим счётчик
endmodule
